# Fritzing sketch circuit (saved by Fritzing 0.9.4)
breadboards: 6

parts:
  LED1 = smd LED [color="White (4500K)" package="0603 [SMD]"]  # not connected
  LED2 = smd LED [color="White (4500K)" package="0603 [SMD]"]  # not connected
  LED3 = smd LED [color="White (4500K)" package="0603 [SMD]"]  # not connected
  LED4 = smd LED [color="Red (633nm)" package="0603 [SMD]"]  # not connected
  LED5 = smd LED [color="Red (633nm)" package="0603 [SMD]"]  # not connected
  LED6 = smd LED [color="Red (633nm)" package="0603 [SMD]"]  # not connected
  LED7 = smd LED [color="Red (633nm)" package="0603 [SMD]"]  # not connected
  LED8 = smd LED [color="Red (633nm)" package="0603 [SMD]"]  # not connected
  LED9 = smd LED [color="White (4500K)" package="0603 [SMD]"]  # not connected
  LED10 = smd LED [color="Red (633nm)" package="0603 [SMD]"]  # not connected
  LED11 = smd LED [color="Red (633nm)" package="0603 [SMD]"]  # not connected
  LED12 = smd LED [color="White (4500K)" package="0603 [SMD]"]  # not connected
  LED13 = smd LED [color="Red (633nm)" package="0603 [SMD]"]  # not connected
  LED14 = smd LED [color="Red (633nm)" package="0603 [SMD]"]  # not connected
  LED15 = smd LED [color="Red (633nm)" package="0603 [SMD]"]  # not connected
  LED16 = smd LED [color="Red (633nm)" package="0603 [SMD]"]  # not connected
  LED17 = smd LED [color="White (4500K)" package="0603 [SMD]"]  # not connected
  LED18 = smd LED [color="Red (633nm)" package="0603 [SMD]"]  # not connected
  LED19 = smd LED [color="Red (633nm)" package="0603 [SMD]"]  # not connected
  LED20 = smd LED [color="White (4500K)" package="0603 [SMD]"]  # not connected
  LED21 = smd LED [color="Red (633nm)" package="0603 [SMD]"]  # not connected
  LED22 = smd LED [color="Red (633nm)" package="0603 [SMD]"]  # not connected
  LED23 = smd LED [color="Red (633nm)" package="0603 [SMD]"]  # not connected
  LED24 = smd LED [color="Red (633nm)" package="0603 [SMD]"]  # not connected
  IC1 = IC, DIP package, 40 pins [chip_label=PIC18F4520]
  S2 = Pushbutton [package="[THT]"]
  S3 = Pushbutton [package="[THT]"]
  S4 = Pushbutton [package="[THT]"]
  S5 = Pushbutton [package="[THT]"]
  S6 = Pushbutton [package="[THT]"]

nets:
  N1: IC1.pin12, S3.Pin_1, S3.Pin_2
  N2: IC1.pin13, S4.Pin_1, S4.Pin_2
  N3: IC1.pin14, S5.Pin_1, S5.Pin_2
  N4: IC1.pin15, S6.Pin_1, S6.Pin_2
  N5: IC1.pin23, S2.Pin_1, S2.Pin_2
  N6: S2.Pin_3, S2.Pin_4
  N7: S3.Pin_3, S3.Pin_4
  N8: S4.Pin_3, S4.Pin_4
  N9: S5.Pin_3, S5.Pin_4
  N10: S6.Pin_3, S6.Pin_4

notes:
  seconds
  minutes
  hours
  hr+ hr- min+ min-
  reset
